// Logisim project Common bus-1.circ as structural Verilog: 2 circuits, main circuit main
module main (
  input  [1:0] Select_line,
  input  [3:0] Input_for_register_D,
  input  [3:0] Input_for_register_C,
  input  [3:0] Input_for_register_B,
  input  [3:0] Input_for_register_A,
  input  CLR,
  output [3:0] Common_bus,
  output [3:0] out_8,
  output [3:0] out_9,
  output [3:0] out_10,
  output [3:0] out_11
);

  wire clock_1_out;

  Multiplexer #(.select(2), .enable("false")) multiplexer_1 (
    .in0(out_11[3]), .in1(out_10[3]), .in2(out_9[3]), .in3(out_8[3]), .out(Common_bus[3]), .sel(Select_line));
  Clock clock_1 (.out(clock_1_out));
  Register #(.width(4)) D (.D(Input_for_register_D), .en(1'b1), .Q(out_8), .clk(clock_1_out), .clr(CLR));
  Multiplexer #(.select(2), .enable("false")) multiplexer_2 (
    .in0(out_11[2]), .in1(out_10[2]), .in2(out_9[2]), .in3(out_8[2]), .out(Common_bus[2]), .sel(Select_line));
  Register #(.width(4)) C (.D(Input_for_register_C), .en(1'b1), .Q(out_9), .clk(clock_1_out), .clr(CLR));
  Multiplexer #(.select(2), .enable("false")) multiplexer_3 (
    .in0(out_11[1]), .in1(out_10[1]), .in2(out_9[1]), .in3(out_8[1]), .out(Common_bus[1]), .sel(Select_line));
  Register #(.width(4)) B (.D(Input_for_register_B), .en(1'b1), .Q(out_10), .clk(clock_1_out), .clr(CLR));
  Multiplexer #(.select(2), .enable("false")) multiplexer_4 (
    .in0(out_11[0]), .in1(out_10[0]), .in2(out_9[0]), .in3(out_8[0]), .out(Common_bus[0]), .sel(Select_line));
  Register #(.width(4)) A (.D(Input_for_register_A), .en(1'b1), .Q(out_11), .clk(clock_1_out), .clr(CLR));

  // Notes on the sheet:
  //   Select line 00: A
  //   Select line 01: B
  //   Select line 10: C
  //   Select line 11: D
  //   23CS053
  //   Bit 3
  //   Bit 2
  //   Bit 1
  //   Bit 0
endmodule

module circ_2 (
  input  [1:0] Select_line,
  input  [3:0] Input_for_register_D,
  input  [3:0] Input_for_register_C,
  input  [3:0] Input_for_register_B,
  input  [3:0] Input_for_register_A,
  input  CLR,
  output [3:0] Common_bus,
  output [3:0] out_8,
  output [3:0] out_9,
  output [3:0] out_10,
  output [3:0] out_11
);

  wire clock_1_out, decoder_1_out0, decoder_1_out1, decoder_1_out2, decoder_1_out3;

  Decoder #(.select(2), .enable("false")) decoder_1 (
    .out0(decoder_1_out0), .out1(decoder_1_out1), .out2(decoder_1_out2), .out3(decoder_1_out3),
    .sel(Select_line));
  Clock clock_1 (.out(clock_1_out));
  Register #(.width(4)) D (.D(Input_for_register_D), .en(1'b1), .Q(out_8), .clk(clock_1_out), .clr(CLR));
  assign Common_bus[3] = decoder_1_out0 ? out_11[3] : 1'bz;  // Controlled_Buffer controlled_buffer_1
  assign Common_bus[2] = decoder_1_out0 ? out_11[2] : 1'bz;  // Controlled_Buffer controlled_buffer_2
  assign Common_bus[2] = decoder_1_out1 ? out_10[2] : 1'bz;  // Controlled_Buffer controlled_buffer_3
  assign Common_bus[3] = decoder_1_out1 ? out_10[3] : 1'bz;  // Controlled_Buffer controlled_buffer_4
  assign Common_bus[3] = decoder_1_out2 ? out_9[3] : 1'bz;  // Controlled_Buffer controlled_buffer_5
  assign Common_bus[2] = decoder_1_out2 ? out_9[2] : 1'bz;  // Controlled_Buffer controlled_buffer_6
  assign Common_bus[2] = decoder_1_out3 ? out_8[2] : 1'bz;  // Controlled_Buffer controlled_buffer_7
  assign Common_bus[3] = decoder_1_out3 ? out_8[3] : 1'bz;  // Controlled_Buffer controlled_buffer_8
  Register #(.width(4)) C (.D(Input_for_register_C), .en(1'b1), .Q(out_9), .clk(clock_1_out), .clr(CLR));
  assign Common_bus[1] = decoder_1_out0 ? out_11[1] : 1'bz;  // Controlled_Buffer controlled_buffer_9
  assign Common_bus[1] = decoder_1_out1 ? out_10[1] : 1'bz;  // Controlled_Buffer controlled_buffer_10
  assign Common_bus[1] = decoder_1_out2 ? out_9[1] : 1'bz;  // Controlled_Buffer controlled_buffer_11
  assign Common_bus[1] = decoder_1_out3 ? out_8[1] : 1'bz;  // Controlled_Buffer controlled_buffer_12
  assign Common_bus[0] = decoder_1_out0 ? out_11[0] : 1'bz;  // Controlled_Buffer controlled_buffer_13
  assign Common_bus[0] = decoder_1_out1 ? out_10[0] : 1'bz;  // Controlled_Buffer controlled_buffer_14
  assign Common_bus[0] = decoder_1_out2 ? out_9[0] : 1'bz;  // Controlled_Buffer controlled_buffer_15
  assign Common_bus[0] = decoder_1_out3 ? out_8[0] : 1'bz;  // Controlled_Buffer controlled_buffer_16
  Register #(.width(4)) B (.D(Input_for_register_B), .en(1'b1), .Q(out_10), .clk(clock_1_out), .clr(CLR));
  Register #(.width(4)) A (.D(Input_for_register_A), .en(1'b1), .Q(out_11), .clk(clock_1_out), .clr(CLR));

  // Notes on the sheet:
  //   23CS053
  //   A3
  //   B3
  //   C3
  //   D3
  //   A2
  //   B2
  //   C2
  //   D2
  //   A1
  //   B1
  //   C1
  //   D1
  //   A0
  //   B0
  //   C0
  //   D0
endmodule
